// Logisim project DDCA Project.circ as structural Verilog: 1 circuit, main circuit main
module main (
  input  EMERGENCY,
  input  ABNORMAL,
  input  ABNORMAL_2,
  input  LOW
);

  wire not_1_out, or_1_out, or_2_out;

  or or_1 (or_1_out, EMERGENCY, ABNORMAL, ABNORMAL_2);
  or or_2 (or_2_out, ABNORMAL_2, ABNORMAL_2, LOW);
  not not_1 (not_1_out, or_1_out);
  LED led_1 (.in(or_1_out));
  LED led_2 (.in(not_1_out));
  LED led_3 (.in(or_2_out));

  // Notes on the sheet:
  //   PANIC BUTTON
  //   TEMPERATURE
  //   HEART RATE
  //   OXYGEN LEVEL
endmodule
